# Fritzing sketch collector (saved by Fritzing 0.8.3b)
circuit board: 5cm x 3.1cm

parts:
  SPI = male pin header, 5 pins [form="♂ (male)"]
  Rot = male pin header, 9 pins [form="♂ (male)"]
  Accel = male pin header, 9 pins [form="♂ (male)"]
  S1 = double row rounded female pin header, 12 pins [form="♀ (female rounded)"]
  S2 = double row rounded female pin header, 12 pins [form="♀ (female rounded)"]
  C1 = Ceramic Capacitor [capacitance=1µF voltage=10V package="100 mil [THT, multilayer]"]
  C2 = Ceramic Capacitor [capacitance=1µF voltage=10V package="100 mil [THT, multilayer]"]
  C3 = Ceramic Capacitor [capacitance=1µF voltage=10V package="100 mil [THT, multilayer]"]
  C4 = Ceramic Capacitor [capacitance=1µF voltage=10V package="100 mil [THT, multilayer]"]
  C5 = Ceramic Capacitor [capacitance=1µF voltage=10V package="100 mil [THT, multilayer]"]
  C6 = Ceramic Capacitor [capacitance=1µF voltage=10V package="100 mil [THT, multilayer]"]
  I/O1 = rounded female pin header, 6 pins [form="♀ (female rounded)"]
  I/O2 = rounded female pin header, 6 pins [form="♀ (female rounded)"]
  5V = Battery

nets:
  N1: SPI.pin1, Rot.pin6
  N2: SPI.pin2, Rot.pin9, Accel.pin9
  N3: SPI.pin3, Rot.pin8, Accel.pin8
  N4: SPI.pin4, Rot.pin7, Accel.pin7
  N5: SPI.pin5, Accel.pin6
  N6: Rot.pin1, Accel.pin1, S1.pin7, S1.pin9, S1.pin11, S2.pin7, S2.pin9, S2.pin11, C1.0, C2.0, C3.0, C4.0, C5.0, C6.0, 5V.+
  N7: Rot.pin3, Accel.pin3, S1.pin8, S1.pin10, S1.pin12, S2.pin8, S2.pin10, S2.pin12, C1.1, C2.1, C3.1, C4.1, C5.1, C6.1, 5V.-
  N8: S1.pin1, I/O1.pin1
  N9: S1.pin2, I/O1.pin2
  N10: S1.pin3, I/O1.pin3
  N11: S1.pin4, I/O1.pin4
  N12: S1.pin5, I/O1.pin5
  N13: S1.pin6, I/O1.pin6
  N14: S2.pin1, I/O2.pin1
  N15: S2.pin2, I/O2.pin2
  N16: S2.pin3, I/O2.pin3
  N17: S2.pin4, I/O2.pin4
  N18: S2.pin5, I/O2.pin5
  N19: S2.pin6, I/O2.pin6
